# Fritzing sketch HC-05 Connection (saved by Fritzing 0.9.2b)

parts:
  Part1 = Bluetooth HC-05 Macho
  Part2 = Arduino Uno (Rev3) - ICSP

nets:
  N1: Part1.TXD, Part2.D0/RX
  N2: Part1.RXD, Part2.D1/TX
  VCC: Part1.VCC, Part2.3V3
  GND: Part1.GND, Part2.GND

notes:
  Connection List:
  VCC = 3.3V {RED}
  GND = GROUND {BLACK}
  TXD = RXD (digital 0){ORANGE}
  RXD = TXD (digital 1){GREEN}
