# Fritzing sketch GestureSensor (saved by Fritzing 0.9.2b)

parts:
  PART1 = APDS-9960 RGB and Gesture Sensor [part_number=SEN-12787]
  Part1 = Arduino Uno (Rev3) - ICSP

nets:
  VCC: PART1.VCC, Part1.3V3
  GND: PART1.GND, Part1.GND
  N1: PART1.SDA, Part1.A4/SDA
  N2: PART1.SCL, Part1.A5/SCL
  N3: PART1.INT, Part1.D2

notes:
  Connection List
  GND = GND {BLACK}
  VCC = 3.3V {RED}
  SDA = analog 4 {GREY}
  SCL = analog 5 {GREY}
  INT = digital 2 {GREEN}

custom parts:
  APDS-9960 RGB and Gesture Sensor: Breakout board for the Avago APDS-9960 proximity, light, RGB, and gesture sensors. Please visit www.sparkfun.com to learn more.
