# Fritzing sketch neopixelconnection (saved by Fritzing 0.9.2b)

parts:
  neopixel1 = Neopixel 24 Ring
  Part1 = Arduino Uno (Rev3)

nets:
  GND: neopixel1.GND, Part1.GND
  N1: neopixel1.IN, Part1.D6_PWM
  VCC: neopixel1.Vcc, Part1.5V

notes:
  PWR = 5V {RED}
  GND = GND {BLACK}
  DATA IN = digital 6 {GREEN}
